# Fritzing sketch ir_sensor_lm311_pot (saved by Fritzing 0.9.3b)
breadboards: 1

parts:
  Raspberry_Pi1 = Raspberry Pi B rev2
  U1 = POT [package=pot_alpha_rv16af-20]
  U2 = LM 311 [package="DIP8 [THT]"]
  R2 = Resistor [tolerance=±5% resistance=1k package="2512 [SMD]"]
  Q2 = LTR-301 [package=ltr-301]

nets:
  N1: Raspberry_Pi1.3V3, U1.A, U2.connector7, R2.Pin_1
  N2: Raspberry_Pi1.GND, U1.E, U2.connector3
  N3: Raspberry_Pi1.GPIO_18, U2.connector0
  N4: U1.S, U2.connector1
  N5: U2.connector2, Q2.E
  N6: R2.Pin_0, Q2.C

notes:
  This is not a lm 358, but a LM311

custom parts:
  LM 311: lm 311
