# Fritzing sketch led_lm311_pot (saved by Fritzing 0.9.3b)
breadboards: 1

parts:
  Raspberry_Pi1 = Raspberry Pi B rev2
  U1 = POT [package=pot_alpha_rv16af-20]
  U2 = LM 311 [package="DIP8 [THT]"]
  R1 = Resistor [tolerance=±5% resistance=220 package="2512 [SMD]"]
  LED1 = LED - 5mm [color="Red (633nm)" package="5 mm [THT]"]

nets:
  N1: Raspberry_Pi1.3V3, U2.connector2
  N2: Raspberry_Pi1.5V, U1.A, U2.connector7
  N3: Raspberry_Pi1.GND, U1.E, U2.connector3, R1.Pin_0
  N4: U1.S, U2.connector1
  N5: U2.connector0, LED1.anode
  N6: R1.Pin_1, LED1.cathode

notes:
  This is not a lm 358, but a LM311

custom parts:
  LM 311: lm 311
