# Fritzing sketch ir_sensor_rc (saved by Fritzing 0.9.3b)
breadboards: 2

parts:
  R1 = Resistor [tolerance=±5% resistance=1k package="2512 [SMD]"]
  C1 = Electrolytic Capacitor [capacitance=10µF package="1010 [SMD, electrolytic]"]
  Raspberry_Pi1 = Raspberry Pi B rev2
  R2 = Resistor [tolerance=±5% resistance=280 package="2512 [SMD]"]
  LED1 = LED - 5mm [color="Infrared (850nm)" package="5 mm [THT]"]
  Q1 = LTR-301 [package=ltr-301]

nets:
  N1: R1.Pin_0, Q1.C
  N2: R1.Pin_1, Raspberry_Pi1.3V3, Raspberry_Pi1.GPIO_2
  N3: C1.+, Raspberry_Pi1.GPIO_24, Q1.E
  N4: Raspberry_Pi1.5V, R2.Pin_0
  N5: Raspberry_Pi1.GND, LED1.cathode
  N6: R2.Pin_1, LED1.anode

notes:
  using til78 I had to plug the collector on the resistor
