# Fritzing sketch ir_sensor_rc_multiple (saved by Fritzing 0.9.3b)
breadboards: 4

parts:
  R1 = Resistor [tolerance=±5% resistance=1k package="2512 [SMD]"]
  C1 = Electrolytic Capacitor [capacitance=10µF package="1010 [SMD, electrolytic]"]
  Raspberry_Pi1 = Raspberry Pi B rev2
  R2 = Resistor [tolerance=±5% resistance=280 package="2512 [SMD]"]
  LED1 = LED - 5mm [color="Infrared (850nm)" package="5 mm [THT]"]
  Q1 = LTR-301 [package=ltr-301]
  R3 = Resistor [tolerance=±5% resistance=1k package="2512 [SMD]"]
  C2 = Electrolytic Capacitor [capacitance=10µF package="1010 [SMD, electrolytic]"]
  Q2 = LTR-301 [package=ltr-301]
  R4 = Resistor [tolerance=±5% resistance=1k package="2512 [SMD]"]
  R5 = Resistor [tolerance=±5% resistance=1k package="2512 [SMD]"]
  C3 = Electrolytic Capacitor [capacitance=1µF package="1010 [SMD, electrolytic]"]
  Q3 = LTR-301 [package=ltr-301]
  Q4 = LTR-301 [package=ltr-301]
  Raspberry_Pi2 = Raspberry Pi B rev2
  R6 = Resistor [tolerance=±5% resistance=1k package="2512 [SMD]"]
  R7 = Resistor [tolerance=±5% resistance=1k package="2512 [SMD]"]
  C4 = Electrolytic Capacitor [capacitance=1µF package="1010 [SMD, electrolytic]"]
  Q5 = LTR-301 [package=ltr-301]
  Q6 = LTR-301 [package=ltr-301]

nets:
  N1: R1.Pin_0, Q1.C
  N2: R1.Pin_1, Raspberry_Pi1.3V3, Raspberry_Pi1.GPIO_2, R3.Pin_1
  N3: C1.-, Raspberry_Pi1.GND, LED1.cathode, C2.-
  N4: C1.+, Raspberry_Pi1.GPIO_24, Q1.E, C2.+, Q2.E
  N5: Raspberry_Pi1.5V, R2.Pin_0
  N6: R2.Pin_1, LED1.anode
  N7: R3.Pin_0, Q2.C
  N8: R4.Pin_0, Q3.C
  N9: R4.Pin_1, R5.Pin_1, Raspberry_Pi2.3V3
  N10: R5.Pin_0, Q4.C
  N11: C3.-, Raspberry_Pi2.GND
  N12: C3.+, Q3.E, Q4.E, Raspberry_Pi2.GPIO_24
  N13: R6.Pin_0, Q6.C
  N14: R7.Pin_0, Q5.C
  N15: C4.+, Q5.E
