# Fritzing sketch layout_opto (saved by Fritzing 0.9.3b)
breadboards: 1

parts:
  Raspberry_Pi1 = Raspberry Pi B rev2
  U1 = TLP621 [package=THT]
  R1 = Resistor [tolerance=±5% resistance=220 package=THT]
  Q2 = NPN-Transistor [package="TO92 [THT]"]
  R2 = Resistor [tolerance=±5% resistance=10k package=THT]
  LED1 = LED - 3mm [color="Red (633nm)" package="3 mm [THT]"]
  R3 = Resistor [tolerance=±5% resistance=220 package=THT]
  VCC1 = Battery block 9V

nets:
  N1: Raspberry_Pi1.5V, R1.Pin_1
  N2: Raspberry_Pi1.GPIO_24, R2.Pin_1
  N3: Raspberry_Pi1.GND, Q2.E
  N4: U1.Pin_1, R1.Pin_0
  N5: U1.Pin_2, Q2.C
  N6: U1.Pin_4, VCC1.+
  N7: U1.Pin_3, LED1.anode
  N8: Q2.B, R2.Pin_0
  N9: LED1.cathode, R3.Pin_1
  N10: R3.Pin_0, VCC1.-
